// Logisim project computer.circ as structural Verilog: 6 circuits, main circuit main
module main (
  input  in_1,
  input  [4:0] in_2,
  input  in_3,
  input  in_4,
  input  in_5,
  input  [7:0] in_6,
  input  [7:0] in_7,
  input  in_8,
  input  in_9,
  input  in_10,
  input  in_11,
  output [7:0] out_12,
  output out_13,
  output out_14,
  output [4:0] out_15,
  output [7:0] out_16,
  output [7:0] out_17,
  output [7:0] out_18,
  output [7:0] out_19
);

  wire clock_13_out, clock_21_out, decoder_1_out0, decoder_1_out1, decoder_1_out2, decoder_1_out3,
       decoder_1_out4, decoder_1_out5, decoder_1_out6, decoder_1_out7, decoder_1_out8, decoder_1_out9,
       decoder_1_out10, decoder_1_out11, decoder_1_out12, decoder_1_out13, decoder_1_out14, decoder_1_out15,
       decoder_1_out16, decoder_1_out17, decoder_1_out18, decoder_1_out19, decoder_1_out20, decoder_1_out21,
       decoder_1_out22, decoder_1_out23, decoder_1_out24, decoder_1_out25, decoder_1_out26, decoder_1_out27,
       decoder_1_out28, decoder_1_out29, decoder_1_out30, decoder_1_out31, demultiplexer_1_out0,
       demultiplexer_1_out1, demultiplexer_2_out0, demultiplexer_2_out1, demultiplexer_3_out0,
       demultiplexer_3_out1, demultiplexer_4_out0, demultiplexer_4_out1, demultiplexer_5_out0,
       demultiplexer_5_out1;
  wire [4:0] controlled_buffer_1_out;
  wire [7:0] controlled_buffer_3_out, controlled_buffer_7_out;

  Demultiplexer demultiplexer_1 (.out0(demultiplexer_1_out0), .out1(demultiplexer_1_out1), .in(1'b1), .sel(in_1));
  Clock clock_1 (.out(out_15[0]));
  Clock #(.highDuration(2), .lowDuration(2)) clock_2 (.out(out_15[1]));
  Clock #(.highDuration(4), .lowDuration(4)) clock_3 (.out(out_15[2]));
  Clock #(.highDuration(8), .lowDuration(8)) clock_4 (.out(out_15[3]));
  Clock #(.highDuration(16), .lowDuration(16)) clock_5 (.out(out_15[4]));
  Decoder #(.enable("false"), .select(5)) decoder_1 (
    .out0(decoder_1_out0), .out1(decoder_1_out1), .out2(decoder_1_out2), .out3(decoder_1_out3),
    .out4(decoder_1_out4), .out5(decoder_1_out5), .out6(decoder_1_out6), .out7(decoder_1_out7),
    .out8(decoder_1_out8), .out9(decoder_1_out9), .out10(decoder_1_out10), .out11(decoder_1_out11),
    .out12(decoder_1_out12), .out13(decoder_1_out13), .out14(decoder_1_out14), .out15(decoder_1_out15),
    .out16(decoder_1_out16), .out17(decoder_1_out17), .out18(decoder_1_out18), .out19(decoder_1_out19),
    .out20(decoder_1_out20), .out21(decoder_1_out21), .out22(decoder_1_out22), .out23(decoder_1_out23),
    .out24(decoder_1_out24), .out25(decoder_1_out25), .out26(decoder_1_out26), .out27(decoder_1_out27),
    .out28(decoder_1_out28), .out29(decoder_1_out29), .out30(decoder_1_out30), .out31(decoder_1_out31),
    .sel(controlled_buffer_1_out));
  assign controlled_buffer_1_out = demultiplexer_1_out0 ? out_15 : 5'bz;  // Controlled_Buffer controlled_buffer_1
  Pull_Resistor pull_resistor_1 (.node(controlled_buffer_1_out));
  assign controlled_buffer_1_out = demultiplexer_1_out1 ? in_2 : 5'bz;  // Controlled_Buffer controlled_buffer_2
  Demultiplexer demultiplexer_2 (.out0(demultiplexer_2_out0), .out1(demultiplexer_2_out1), .in(1'b1), .sel(in_4));
  Clock clock_6 (.out(out_16[0]));
  Clock #(.highDuration(2), .lowDuration(2)) clock_7 (.out(out_16[1]));
  Clock #(.highDuration(4), .lowDuration(4)) clock_8 (.out(out_16[2]));
  Clock #(.highDuration(8), .lowDuration(8)) clock_9 (.out(out_16[3]));
  Clock #(.highDuration(16), .lowDuration(16)) clock_10 (.out(out_16[4]));
  Clock #(.highDuration(32), .lowDuration(32)) clock_11 (.out(out_16[5]));
  Clock #(.highDuration(64), .lowDuration(64)) clock_12 (.out(out_16[6]));
  Demultiplexer demultiplexer_3 (.out0(demultiplexer_3_out0), .out1(demultiplexer_3_out1), .in(1'b1), .sel(in_10));
  Clock #(.highDuration(128), .lowDuration(128)) clock_13 (.out(clock_13_out));
  assign controlled_buffer_3_out = demultiplexer_2_out0 ? out_16 : 8'bz;  // Controlled_Buffer controlled_buffer_3
  assign controlled_buffer_3_out = demultiplexer_2_out1 ? in_6 : 8'bz;  // Controlled_Buffer controlled_buffer_4
  assign out_16[7] = demultiplexer_3_out0 ? clock_13_out : 1'bz;  // Controlled_Buffer controlled_buffer_5
  assign out_16[7] = demultiplexer_3_out1 ? in_8 : 1'bz;  // Controlled_Buffer controlled_buffer_6
  Pull_Resistor pull_resistor_2 (.node(out_16[7]));
  Clock #(.highDuration(256), .lowDuration(256)) clock_14 (.out(out_17[0]));
  Clock #(.highDuration(512), .lowDuration(512)) clock_15 (.out(out_17[1]));
  Clock #(.highDuration(1024), .lowDuration(1024)) clock_16 (.out(out_17[2]));
  Clock #(.highDuration(2048), .lowDuration(2048)) clock_17 (.out(out_17[3]));
  Clock #(.highDuration(4096), .lowDuration(4096)) clock_18 (.out(out_17[4]));
  Clock #(.highDuration(8192), .lowDuration(8192)) clock_19 (.out(out_17[5]));
  Clock #(.highDuration(16384), .lowDuration(16384)) clock_20 (.out(out_17[6]));
  Demultiplexer demultiplexer_4 (.out0(demultiplexer_4_out0), .out1(demultiplexer_4_out1), .in(1'b1), .sel(in_11));
  assign controlled_buffer_7_out = demultiplexer_5_out0 ? out_17 : 8'bz;  // Controlled_Buffer controlled_buffer_7
  Demultiplexer demultiplexer_5 (.out0(demultiplexer_5_out0), .out1(demultiplexer_5_out1), .in(1'b1), .sel(in_5));
  assign out_17[7] = demultiplexer_4_out0 ? clock_21_out : 1'bz;  // Controlled_Buffer controlled_buffer_8
  Clock #(.highDuration(32768), .lowDuration(32768)) clock_21 (.out(clock_21_out));
  assign controlled_buffer_7_out = demultiplexer_5_out1 ? in_7 : 8'bz;  // Controlled_Buffer controlled_buffer_9
  Pull_Resistor pull_resistor_3 (.node(out_17[7]));
  assign out_17[7] = demultiplexer_4_out1 ? in_9 : 1'bz;  // Controlled_Buffer controlled_buffer_10
  ALU alu_1 (
    .non(decoder_1_out10), .et(decoder_1_out9), .ou(decoder_1_out8), .non_et(decoder_1_out7),
    .non_ou(decoder_1_out6), .ou_exclusif(decoder_1_out5), .non_ou_exclusif(decoder_1_out4),
    .div(decoder_1_out3), .mul(decoder_1_out2), .sub(decoder_1_out1), .add(decoder_1_out0), .C_in(in_3),
    .A(controlled_buffer_3_out), .B(controlled_buffer_7_out), .Res(out_12), .C_over_add(out_13),
    .C_under_sub(out_14));  // open: C_under_mul, C_under_div

  assign out_18 = out_16;
  assign out_19 = out_17;

  // Notes on the sheet:
  //   in_1: initial=0x1
endmodule

module ALU (
  input  non,
  input  et,
  input  ou,
  input  non_et,
  input  non_ou,
  input  ou_exclusif,
  input  non_ou_exclusif,
  input  div,
  input  mul,
  input  sub,
  input  add,
  input  C_in,
  input  [7:0] A,
  input  [7:0] B,
  output [7:0] Res,
  output C_over_add,
  output C_under_sub,
  output C_under_mul,
  output C_under_div
);

  wire alu_add_8bits_1_c_out, alu_div_8bits_1_c_out, alu_mul_8bits_1_c_out, alu_sub_8bits_1_c_out;
  wire [7:0] alu_add_8bits_1_res, alu_div_8bits_1_res, alu_mul_8bits_1_res, alu_sub_8bits_1_res, and_1_out,
       nand_1_out, nor_1_out, not_1_out, or_1_out, xnor_1_out, xor_1_out;

  assign not_1_out = ~A;  // NOT_Gate not_1, 8 bits wide
  assign xnor_1_out = ~(A ^ B);  // XNOR_Gate xnor_1, 8 bits wide
  assign xor_1_out = A ^ B;  // XOR_Gate xor_1, 8 bits wide
  assign nor_1_out = ~(A | B);  // NOR_Gate nor_1, 8 bits wide
  assign nand_1_out = ~(A & B);  // NAND_Gate nand_1, 8 bits wide
  assign or_1_out = A | B;  // OR_Gate or_1, 8 bits wide
  assign and_1_out = A & B;  // AND_Gate and_1, 8 bits wide
  assign Res = add ? alu_add_8bits_1_res : 8'bz;  // Controlled_Buffer controlled_buffer_1
  ALU_add_8bits alu_add_8bits_1 (.C_in(C_in), .A(A), .B(B), .Res(alu_add_8bits_1_res), .C_out(alu_add_8bits_1_c_out));
  assign C_over_add = add ? alu_add_8bits_1_c_out : 1'bz;  // Controlled_Buffer controlled_buffer_2
  assign Res = sub ? alu_sub_8bits_1_res : 8'bz;  // Controlled_Buffer controlled_buffer_3
  ALU_sub_8bits alu_sub_8bits_1 (.C_in(C_in), .A(A), .B(B), .res(alu_sub_8bits_1_res), .C_out(alu_sub_8bits_1_c_out));
  assign C_under_sub = sub ? alu_sub_8bits_1_c_out : 1'bz;  // Controlled_Buffer controlled_buffer_4
  ALU_mul_8bits alu_mul_8bits_1 (.C_in(C_in), .A(A), .B(B), .res(alu_mul_8bits_1_res), .C_out(alu_mul_8bits_1_c_out));
  ALU_div_8bits alu_div_8bits_1 (.C_in(C_in), .A(A), .B(B), .res(alu_div_8bits_1_res), .C_out(alu_div_8bits_1_c_out));
  assign Res = mul ? alu_mul_8bits_1_res : 8'bz;  // Controlled_Buffer controlled_buffer_5
  assign C_under_mul = mul ? alu_mul_8bits_1_c_out : 1'bz;  // Controlled_Buffer controlled_buffer_6
  assign Res = div ? alu_div_8bits_1_res : 8'bz;  // Controlled_Buffer controlled_buffer_7
  assign C_under_div = div ? alu_div_8bits_1_c_out : 1'bz;  // Controlled_Buffer controlled_buffer_8
  assign Res = non_ou_exclusif ? xnor_1_out : 8'bz;  // Controlled_Buffer controlled_buffer_9
  assign Res = ou_exclusif ? xor_1_out : 8'bz;  // Controlled_Buffer controlled_buffer_10
  assign Res = non_ou ? nor_1_out : 8'bz;  // Controlled_Buffer controlled_buffer_11
  assign Res = non_et ? nand_1_out : 8'bz;  // Controlled_Buffer controlled_buffer_12
  assign Res = ou ? or_1_out : 8'bz;  // Controlled_Buffer controlled_buffer_13
  assign Res = et ? and_1_out : 8'bz;  // Controlled_Buffer controlled_buffer_14
  assign Res = non ? not_1_out : 8'bz;  // Controlled_Buffer controlled_buffer_15
  Pull_Resistor pull_resistor_1 (.node(Res));
  Pull_Resistor pull_resistor_2 (.node(C_over_add));
  Pull_Resistor pull_resistor_3 (.node(C_under_sub));
  Pull_Resistor pull_resistor_4 (.node(C_under_mul));
  Pull_Resistor pull_resistor_5 (.node(C_under_div));
endmodule

module ALU_add_8bits (
  input  C_in,
  input  [7:0] A,
  input  [7:0] B,
  output [7:0] Res,
  output C_out
);

  wire and_1_out, and_2_out, and_3_out, and_4_out, and_5_out, and_6_out, and_7_out, and_8_out, and_9_out,
       and_10_out, and_11_out, and_12_out, and_13_out, and_14_out, and_15_out, and_16_out, or_1_out,
       or_2_out, or_3_out, or_4_out, or_5_out, or_6_out, or_7_out, xor_1_out, xor_2_out, xor_3_out,
       xor_4_out, xor_5_out, xor_6_out, xor_7_out, xor_8_out;

  xor xor_1 (xor_1_out, A[0], B[0]);
  xor xor_2 (xor_2_out, A[1], B[1]);
  xor xor_3 (xor_3_out, A[2], B[2]);
  xor xor_4 (xor_4_out, A[3], B[3]);
  xor xor_5 (xor_5_out, A[4], B[4]);
  xor xor_6 (xor_6_out, A[5], B[5]);
  xor xor_7 (xor_7_out, A[6], B[6]);
  xor xor_8 (xor_8_out, A[7], B[7]);
  xor xor_9 (Res[0], xor_1_out, C_in);
  and and_1 (and_1_out, C_in, xor_1_out);
  and and_2 (and_2_out, A[0], B[0]);
  xor xor_10 (Res[1], xor_2_out, or_1_out);
  and and_3 (and_3_out, or_1_out, xor_2_out);
  and and_4 (and_4_out, A[1], B[1]);
  xor xor_11 (Res[2], xor_3_out, or_2_out);
  and and_5 (and_5_out, or_2_out, xor_3_out);
  and and_6 (and_6_out, A[2], B[2]);
  xor xor_12 (Res[3], xor_4_out, or_3_out);
  and and_7 (and_7_out, or_3_out, xor_4_out);
  and and_8 (and_8_out, A[3], B[3]);
  xor xor_13 (Res[4], xor_5_out, or_4_out);
  and and_9 (and_9_out, or_4_out, xor_5_out);
  and and_10 (and_10_out, A[4], B[4]);
  xor xor_14 (Res[5], xor_6_out, or_5_out);
  and and_11 (and_11_out, or_5_out, xor_6_out);
  and and_12 (and_12_out, A[5], B[5]);
  xor xor_15 (Res[6], xor_7_out, or_6_out);
  and and_13 (and_13_out, or_6_out, xor_7_out);
  and and_14 (and_14_out, A[6], B[6]);
  xor xor_16 (Res[7], xor_8_out, or_7_out);
  and and_15 (and_15_out, or_7_out, xor_8_out);
  and and_16 (and_16_out, A[7], B[7]);
  or or_1 (or_1_out, and_1_out, and_2_out);
  or or_2 (or_2_out, and_3_out, and_4_out);
  or or_3 (or_3_out, and_5_out, and_6_out);
  or or_4 (or_4_out, and_7_out, and_8_out);
  or or_5 (or_5_out, and_9_out, and_10_out);
  or or_6 (or_6_out, and_11_out, and_12_out);
  or or_7 (or_7_out, and_13_out, and_14_out);
  or or_8 (C_out, and_15_out, and_16_out);
endmodule

module ALU_sub_8bits (
  input  C_in,
  input  [7:0] A,
  input  [7:0] B,
  output [7:0] res,
  output C_out
);

  wire alu_add_8bits_1_c_out, alu_add_8bits_2_c_out;
  wire [7:0] alu_add_8bits_1_res, not_1_out;

  assign not_1_out = ~B;  // NOT_Gate not_1, 8 bits wide
  ALU_add_8bits alu_add_8bits_1 (
    .C_in(C_in), .A(not_1_out), .B(8'h1), .Res(alu_add_8bits_1_res), .C_out(alu_add_8bits_1_c_out));
  ALU_add_8bits alu_add_8bits_2 (.C_in(C_in), .A(A), .B(alu_add_8bits_1_res), .Res(res), .C_out(alu_add_8bits_2_c_out));
  or or_1 (C_out, alu_add_8bits_2_c_out, alu_add_8bits_1_c_out);
endmodule

module ALU_mul_8bits (
  input  C_in,
  input  [7:0] A,
  input  [7:0] B,
  output [7:0] res,
  output C_out
);

  wire alu_add_8bits_1_c_out, alu_add_8bits_2_c_out;
  wire [7:0] alu_add_8bits_1_res, not_1_out;

  assign not_1_out = ~B;  // NOT_Gate not_1, 8 bits wide
  ALU_add_8bits alu_add_8bits_1 (
    .C_in(C_in), .A(not_1_out), .B(8'h1), .Res(alu_add_8bits_1_res), .C_out(alu_add_8bits_1_c_out));
  ALU_add_8bits alu_add_8bits_2 (.C_in(C_in), .A(A), .B(alu_add_8bits_1_res), .Res(res), .C_out(alu_add_8bits_2_c_out));
  or or_1 (C_out, alu_add_8bits_2_c_out, alu_add_8bits_1_c_out);
endmodule

module ALU_div_8bits (
  input  C_in,
  input  [7:0] A,
  input  [7:0] B,
  output [7:0] res,
  output C_out
);

  wire alu_add_8bits_1_c_out, alu_add_8bits_2_c_out;
  wire [7:0] alu_add_8bits_1_res, not_1_out;

  assign not_1_out = ~B;  // NOT_Gate not_1, 8 bits wide
  ALU_add_8bits alu_add_8bits_1 (
    .C_in(C_in), .A(not_1_out), .B(8'h1), .Res(alu_add_8bits_1_res), .C_out(alu_add_8bits_1_c_out));
  ALU_add_8bits alu_add_8bits_2 (.C_in(C_in), .A(A), .B(alu_add_8bits_1_res), .Res(res), .C_out(alu_add_8bits_2_c_out));
  or or_1 (C_out, alu_add_8bits_2_c_out, alu_add_8bits_1_c_out);
endmodule
