// Logisim project alu.circ as structural Verilog
module main (
);

  add add_1 ();  // open: in_4, in_5, in_6, in_7, in_8, in_9, in_10, in_11, in_12, in_13, in_14, in_15, in_16, in_17, in_18, in_19, in_20, in_21, in_22, in_23, in_24, in_25, in_28, in_30, in_1, in_3, in_27, in_29, in_2, in_26, out_31, out_32, out_33, out_36, out_37, out_38, out_39, out_40, out_41, out_42, out_43, out_44, out_34, out_35, out_47, out_48, out_45, out_46
endmodule

module add (
  input  in_1,
  input  in_2,
  input  in_3,
  input  in_4,
  input  in_5,
  input  in_6,
  input  in_7,
  input  in_8,
  input  in_9,
  input  in_10,
  input  in_11,
  input  in_12,
  input  in_13,
  input  in_14,
  input  in_15,
  input  in_16,
  input  in_17,
  input  in_18,
  input  in_19,
  input  in_20,
  input  in_21,
  input  in_22,
  input  in_23,
  input  in_24,
  input  in_25,
  input  in_26,
  input  in_27,
  input  [7:0] in_28,
  input  in_29,
  input  [7:0] in_30,
  output out_31,
  output out_32,
  output out_33,
  output out_34,
  output out_35,
  output out_36,
  output out_37,
  output out_38,
  output out_39,
  output out_40,
  output out_41,
  output out_42,
  output out_43,
  output out_44,
  output out_45,
  output out_46,
  output [7:0] out_47,
  output out_48
);

  wire and_2_out, and_3_out, and_4_out, and_5_out, and_6_out, and_7_out, and_8_out, and_9_out, and_10_out,
       and_11_out, and_12_out, and_13_out, and_14_out, and_15_out, and_16_out, and_17_out, and_18_out,
       and_19_out, and_20_out, and_21_out, and_22_out, and_23_out, and_24_out, and_25_out, and_26_out,
       and_27_out, and_28_out, and_29_out, and_30_out, and_31_out, and_32_out, and_33_out, and_34_out,
       and_35_out, and_36_out, and_37_out, and_38_out, and_39_out, or_2_out, or_4_out, or_5_out, or_6_out,
       or_7_out, or_8_out, or_9_out, or_10_out, or_12_out, or_13_out, or_14_out, or_15_out, or_16_out,
       or_17_out, or_18_out, xor_2_out, xor_4_out, xor_5_out, xor_8_out, xor_9_out, xor_10_out, xor_11_out,
       xor_12_out, xor_13_out, xor_14_out, xor_15_out, xor_24_out, xor_25_out, xor_26_out, xor_27_out,
       xor_28_out, xor_29_out, xor_30_out, xor_31_out;

  xor xor_1 (out_35, in_2, in_26);
  and and_1 (out_34, in_26, in_2);
  xor xor_2 (xor_2_out, in_27, in_29);
  and and_2 (and_2_out, in_3, xor_2_out);
  and and_3 (and_3_out, in_29, in_27);
  xor xor_3 (out_46, xor_2_out, in_3);
  or or_1 (out_45, and_2_out, and_3_out);
  xor xor_4 (xor_4_out, in_7, in_5);
  xor xor_5 (xor_5_out, in_6, in_4);
  xor xor_6 (out_33, xor_4_out, in_8);
  and and_4 (and_4_out, in_8, xor_4_out);
  and and_5 (and_5_out, in_5, in_7);
  xor xor_7 (out_32, xor_5_out, or_2_out);
  and and_6 (and_6_out, or_2_out, xor_5_out);
  and and_7 (and_7_out, in_4, in_6);
  or or_2 (or_2_out, and_4_out, and_5_out);
  or or_3 (out_31, and_6_out, and_7_out);
  xor xor_8 (xor_8_out, in_24, in_16);
  xor xor_9 (xor_9_out, in_23, in_15);
  xor xor_10 (xor_10_out, in_22, in_14);
  xor xor_11 (xor_11_out, in_21, in_13);
  xor xor_12 (xor_12_out, in_20, in_12);
  xor xor_13 (xor_13_out, in_19, in_11);
  xor xor_14 (xor_14_out, in_18, in_10);
  xor xor_15 (xor_15_out, in_17, in_9);
  xor xor_16 (out_36, xor_8_out, in_25);
  and and_8 (and_8_out, in_25, xor_8_out);
  and and_9 (and_9_out, in_16, in_24);
  xor xor_17 (out_37, xor_9_out, or_4_out);
  and and_10 (and_10_out, or_4_out, xor_9_out);
  and and_11 (and_11_out, in_15, in_23);
  xor xor_18 (out_38, xor_10_out, or_5_out);
  and and_12 (and_12_out, or_5_out, xor_10_out);
  and and_13 (and_13_out, in_14, in_22);
  xor xor_19 (out_39, xor_11_out, or_6_out);
  and and_14 (and_14_out, or_6_out, xor_11_out);
  and and_15 (and_15_out, in_13, in_21);
  xor xor_20 (out_40, xor_12_out, or_7_out);
  and and_16 (and_16_out, or_7_out, xor_12_out);
  and and_17 (and_17_out, in_12, in_20);
  xor xor_21 (out_41, xor_13_out, or_8_out);
  and and_18 (and_18_out, or_8_out, xor_13_out);
  and and_19 (and_19_out, in_11, in_19);
  xor xor_22 (out_42, xor_14_out, or_9_out);
  and and_20 (and_20_out, or_9_out, xor_14_out);
  and and_21 (and_21_out, in_10, in_18);
  xor xor_23 (out_43, xor_15_out, or_10_out);
  and and_22 (and_22_out, or_10_out, xor_15_out);
  and and_23 (and_23_out, in_9, in_17);
  or or_4 (or_4_out, and_8_out, and_9_out);
  or or_5 (or_5_out, and_10_out, and_11_out);
  or or_6 (or_6_out, and_12_out, and_13_out);
  or or_7 (or_7_out, and_14_out, and_15_out);
  or or_8 (or_8_out, and_16_out, and_17_out);
  or or_9 (or_9_out, and_18_out, and_19_out);
  or or_10 (or_10_out, and_20_out, and_21_out);
  or or_11 (out_44, and_22_out, and_23_out);
  xor xor_24 (xor_24_out, in_28[0], in_30[0]);
  xor xor_25 (xor_25_out, in_28[1], in_30[1]);
  xor xor_26 (xor_26_out, in_28[2], in_30[2]);
  xor xor_27 (xor_27_out, in_28[3], in_30[3]);
  xor xor_28 (xor_28_out, in_28[4], in_30[4]);
  xor xor_29 (xor_29_out, in_28[5], in_30[5]);
  xor xor_30 (xor_30_out, in_28[6], in_30[6]);
  xor xor_31 (xor_31_out, in_28[7], in_30[7]);
  xor xor_32 (out_47[0], xor_24_out, in_1);
  and and_24 (and_24_out, in_1, xor_24_out);
  and and_25 (and_25_out, in_30[0], in_28[0]);
  xor xor_33 (out_47[1], xor_25_out, or_12_out);
  and and_26 (and_26_out, or_12_out, xor_25_out);
  and and_27 (and_27_out, in_30[1], in_28[1]);
  xor xor_34 (out_47[2], xor_26_out, or_13_out);
  and and_28 (and_28_out, or_13_out, xor_26_out);
  and and_29 (and_29_out, in_30[2], in_28[2]);
  xor xor_35 (out_47[3], xor_27_out, or_14_out);
  and and_30 (and_30_out, or_14_out, xor_27_out);
  and and_31 (and_31_out, in_30[3], in_28[3]);
  xor xor_36 (out_47[4], xor_28_out, or_15_out);
  and and_32 (and_32_out, or_15_out, xor_28_out);
  and and_33 (and_33_out, in_30[4], in_28[4]);
  xor xor_37 (out_47[5], xor_29_out, or_16_out);
  and and_34 (and_34_out, or_16_out, xor_29_out);
  and and_35 (and_35_out, in_30[5], in_28[5]);
  xor xor_38 (out_47[6], xor_30_out, or_17_out);
  and and_36 (and_36_out, or_17_out, xor_30_out);
  and and_37 (and_37_out, in_30[6], in_28[6]);
  xor xor_39 (out_47[7], xor_31_out, or_18_out);
  and and_38 (and_38_out, or_18_out, xor_31_out);
  and and_39 (and_39_out, in_30[7], in_28[7]);
  or or_12 (or_12_out, and_24_out, and_25_out);
  or or_13 (or_13_out, and_26_out, and_27_out);
  or or_14 (or_14_out, and_28_out, and_29_out);
  or or_15 (or_15_out, and_30_out, and_31_out);
  or or_16 (or_16_out, and_32_out, and_33_out);
  or or_17 (or_17_out, and_34_out, and_35_out);
  or or_18 (or_18_out, and_36_out, and_37_out);
  or or_19 (out_48, and_38_out, and_39_out);

  // Notes on the sheet:
  //   in_28: initial=0x8
endmodule
