// Logisim project minus.circ as structural Verilog: 1 circuit, main circuit main
module main (
  input  [7:0] B,
  input  in_2,
  input  [7:0] in_3,
  input  [7:0] A,
  input  [7:0] in_5,
  output [7:0] out_6,
  output [7:0] out_7,
  output [7:0] Resultat,
  output [7:0] out_9,
  output out_10
);

  wire and_1_out, and_2_out, and_3_out, and_4_out, and_5_out, and_6_out, and_7_out, and_8_out, and_9_out,
       and_10_out, and_11_out, and_12_out, and_13_out, and_14_out, and_15_out, and_16_out, not_2_out,
       not_3_out, not_4_out, not_5_out, not_6_out, not_7_out, not_8_out, not_9_out, not_10_out, not_11_out,
       not_12_out, not_13_out, not_14_out, not_15_out, not_16_out, not_17_out, or_1_out, or_2_out, or_3_out,
       or_4_out, or_5_out, or_6_out, or_7_out, xor_1_out, xor_2_out, xor_3_out, xor_4_out, xor_5_out,
       xor_6_out, xor_7_out, xor_8_out;

  assign out_6 = ~B;  // NOT_Gate not_1, 8 bits wide
  Adder adder_1 (.a(out_6), .b(8'h1), .out(out_7));  // open: cin, cout
  Adder adder_2 (.a(out_7), .b(A), .out(Resultat));  // open: cin, cout
  not not_2 (not_2_out, in_3[0]);
  not not_3 (not_3_out, in_3[1]);
  not not_4 (not_4_out, in_3[2]);
  not not_5 (not_5_out, in_3[3]);
  not not_6 (not_6_out, in_3[4]);
  not not_7 (not_7_out, in_3[5]);
  not not_8 (not_8_out, in_3[6]);
  not not_9 (not_9_out, in_3[7]);
  xor xor_1 (xor_1_out, in_3[0], in_5[0]);
  and and_1 (and_1_out, in_5[0], not_2_out);
  xor xor_2 (xor_2_out, in_3[1], in_5[1]);
  and and_2 (and_2_out, in_5[1], not_3_out);
  xor xor_3 (xor_3_out, in_3[2], in_5[2]);
  and and_3 (and_3_out, in_5[2], not_4_out);
  xor xor_4 (xor_4_out, in_3[3], in_5[3]);
  and and_4 (and_4_out, in_5[3], not_5_out);
  xor xor_5 (xor_5_out, in_3[4], in_5[4]);
  and and_5 (and_5_out, in_5[4], not_6_out);
  xor xor_6 (xor_6_out, in_3[5], in_5[5]);
  and and_6 (and_6_out, in_5[5], not_7_out);
  xor xor_7 (xor_7_out, in_3[6], in_5[6]);
  and and_7 (and_7_out, in_5[6], not_8_out);
  xor xor_8 (xor_8_out, in_3[7], in_5[7]);
  and and_8 (and_8_out, in_5[7], not_9_out);
  not not_10 (not_10_out, xor_1_out);
  not not_11 (not_11_out, xor_2_out);
  not not_12 (not_12_out, xor_3_out);
  not not_13 (not_13_out, xor_4_out);
  not not_14 (not_14_out, xor_5_out);
  not not_15 (not_15_out, xor_6_out);
  not not_16 (not_16_out, xor_7_out);
  not not_17 (not_17_out, xor_8_out);
  xor xor_9 (out_9[0], xor_1_out, in_2);
  and and_9 (and_9_out, in_2, not_10_out);
  xor xor_10 (out_9[1], xor_2_out, or_1_out);
  and and_10 (and_10_out, or_1_out, not_11_out);
  xor xor_11 (out_9[2], xor_3_out, or_2_out);
  and and_11 (and_11_out, or_2_out, not_12_out);
  xor xor_12 (out_9[3], xor_4_out, or_3_out);
  and and_12 (and_12_out, or_3_out, not_13_out);
  xor xor_13 (out_9[4], xor_5_out, or_4_out);
  and and_13 (and_13_out, or_4_out, not_14_out);
  xor xor_14 (out_9[5], xor_6_out, or_5_out);
  and and_14 (and_14_out, or_5_out, not_15_out);
  xor xor_15 (out_9[6], xor_7_out, or_6_out);
  and and_15 (and_15_out, or_6_out, not_16_out);
  xor xor_16 (out_9[7], xor_8_out, or_7_out);
  and and_16 (and_16_out, or_7_out, not_17_out);
  or or_1 (or_1_out, and_9_out, and_1_out);
  or or_2 (or_2_out, and_10_out, and_2_out);
  or or_3 (or_3_out, and_11_out, and_3_out);
  or or_4 (or_4_out, and_12_out, and_4_out);
  or or_5 (or_5_out, and_13_out, and_5_out);
  or or_6 (or_6_out, and_14_out, and_6_out);
  or or_7 (or_7_out, and_15_out, and_7_out);
  or or_8 (out_10, and_16_out, and_8_out);

  // Notes on the sheet:
  //   Soustracteur de nombre entier non signé : A-B
endmodule
