// Logisim project logic_gates.circ as structural Verilog: 2 circuits, main circuit main
module main (
  input  A,
  input  A_2,
  input  A_3,
  input  A_4,
  input  A_5,
  input  A_6,
  input  A_7,
  input  A_8,
  input  B,
  input  B_2,
  input  B_3,
  input  B_4,
  input  B_5,
  input  B_6,
  input  A_9,
  input  A_10,
  input  B_7,
  input  B_8,
  input  in_19,
  input  in_20,
  input  in_21,
  input  in_22,
  input  in_23,
  input  in_24,
  input  in_25,
  input  in_26,
  input  in_27,
  input  in_28,
  input  in_29,
  input  in_30,
  output out_31,
  output out_32,
  output out_33,
  output out_34,
  output out_35,
  output out_36,
  output out_37,
  output out_38,
  output out_39,
  output out_40,
  output out_41,
  output out_42,
  output out_43,
  output out_44,
  output out_45,
  output out_46,
  output out_47,
  output out_48,
  output out_49,
  output out_50,
  output out_51,
  output out_52,
  output out_53,
  output out_54,
  output out_55
);

  wire and_2_out, and_4_out, nand_2_out, nand_3_out, nand_4_out, nand_5_out, nand_7_out, nand_8_out,
       nand_9_out, nand_10_out, nor_2_out, nor_3_out, nor_4_out, nor_5_out, nor_7_out, nor_8_out, nor_9_out,
       nor_10_out, or_2_out, or_3_out, pull_resistor_4_node, pull_resistor_8_node, pull_resistor_9_node,
       pull_resistor_11_node, pull_resistor_14_node, pull_resistor_15_node, pull_resistor_17_node,
       pull_resistor_18_node, pull_resistor_20_node, trnsstr_7_out_3, trnsstr_14_out_3, trnsstr_15_out_3,
       trnsstr_22_out_3;

  buf buffer_1 (out_32, A_5);
  trnsstr trnsstr_1 (.in_1(A_5), .in_2(1'b1), .out_3(out_47));
  Pull_Resistor pull_resistor_1 (.node(out_47));
  not not_1 (out_33, A_6);
  Pull_Resistor #(.pull(1)) pull_resistor_2 (.node(out_46));
  trnsstr trnsstr_2 (.in_1(A_6), .in_2(1'b0), .out_3(out_46));
  trnsstr trnsstr_3 (.in_1(B_2), .in_2(1'b1), .out_3(out_38));
  trnsstr trnsstr_4 (.in_1(A_2), .in_2(1'b1), .out_3(out_38));
  or or_1 (out_34, A_2, B_2);
  Pull_Resistor pull_resistor_3 (.node(out_38));
  and and_1 (out_35, A_3, B_3);
  Pull_Resistor pull_resistor_4 (.node(pull_resistor_4_node));
  trnsstr trnsstr_5 (.in_1(A_3), .in_2(1'b1), .out_3(pull_resistor_4_node));
  trnsstr trnsstr_6 (.in_1(B_3), .in_2(pull_resistor_4_node), .out_3(out_39));
  Pull_Resistor pull_resistor_5 (.node(out_39));
  trnsstr trnsstr_7 (.in_1(A), .in_2(1'b1), .out_3(trnsstr_7_out_3));
  trnsstr trnsstr_8 (.in_1(B), .in_2(1'b1), .out_3(trnsstr_7_out_3));
  nor nor_1 (out_31, A, B);
  Pull_Resistor pull_resistor_6 (.node(trnsstr_7_out_3));
  Pull_Resistor #(.pull(1)) pull_resistor_7 (.node(out_37));
  trnsstr trnsstr_9 (.in_1(trnsstr_7_out_3), .in_2(1'b0), .out_3(out_37));
  or or_2 (or_2_out, A_9, B_7);
  not not_2 (out_48, or_2_out);
  Pull_Resistor pull_resistor_8 (.node(pull_resistor_8_node));
  trnsstr trnsstr_10 (.in_1(A_4), .in_2(1'b1), .out_3(pull_resistor_8_node));
  nand nand_1 (out_36, A_4, B_4);
  Pull_Resistor pull_resistor_9 (.node(pull_resistor_9_node));
  trnsstr trnsstr_11 (.in_1(B_4), .in_2(pull_resistor_8_node), .out_3(pull_resistor_9_node));
  and and_2 (and_2_out, A_10, B_8);
  Pull_Resistor #(.pull(1)) pull_resistor_10 (.node(out_40));
  trnsstr trnsstr_12 (.in_1(pull_resistor_9_node), .in_2(1'b0), .out_3(out_40));
  not not_3 (out_49, and_2_out);
  Pull_Resistor pull_resistor_11 (.node(pull_resistor_11_node));
  trnsstr trnsstr_13 (.in_1(A_7), .in_2(1'b1), .out_3(pull_resistor_11_node));
  trnsstr trnsstr_14 (.in_1(B_5), .in_2(pull_resistor_11_node), .out_3(trnsstr_14_out_3));
  trnsstr trnsstr_15 (.in_1(A_7), .in_2(1'b1), .out_3(trnsstr_15_out_3));
  trnsstr trnsstr_16 (.in_1(B_5), .in_2(1'b1), .out_3(trnsstr_15_out_3));
  nand nand_2 (nand_2_out, in_23, in_25);
  xor xor_1 (out_41, A_7, B_5);
  Pull_Resistor pull_resistor_12 (.node(trnsstr_14_out_3));
  Pull_Resistor pull_resistor_13 (.node(trnsstr_15_out_3));
  nand nand_3 (nand_3_out, in_19, in_21);
  or or_3 (or_3_out, in_19, in_21);
  nand nand_4 (nand_4_out, in_23, nand_2_out);
  nand nand_5 (nand_5_out, nand_2_out, in_25);
  nor nor_2 (nor_2_out, in_27, in_27);
  nor nor_3 (nor_3_out, in_29, in_29);
  nor nor_4 (nor_4_out, in_29, in_27);
  Pull_Resistor #(.pull(1)) pull_resistor_14 (.node(pull_resistor_14_node));
  trnsstr trnsstr_17 (.in_1(trnsstr_14_out_3), .in_2(1'b0), .out_3(pull_resistor_14_node));
  and and_3 (out_50, nand_3_out, or_3_out);
  nand nand_6 (out_52, nand_4_out, nand_5_out);
  nor nor_5 (nor_5_out, nor_2_out, nor_3_out);
  Pull_Resistor pull_resistor_15 (.node(pull_resistor_15_node));
  trnsstr trnsstr_18 (.in_1(trnsstr_15_out_3), .in_2(1'b1), .out_3(pull_resistor_15_node));
  nor nor_6 (out_55, nor_5_out, nor_4_out);
  Pull_Resistor pull_resistor_16 (.node(out_44));
  trnsstr trnsstr_19 (.in_1(pull_resistor_14_node), .in_2(pull_resistor_15_node), .out_3(out_44));
  Pull_Resistor pull_resistor_17 (.node(pull_resistor_17_node));
  Pull_Resistor pull_resistor_18 (.node(pull_resistor_18_node));
  trnsstr trnsstr_20 (.in_1(A_8), .in_2(1'b1), .out_3(pull_resistor_17_node));
  trnsstr trnsstr_21 (.in_1(B_6), .in_2(pull_resistor_17_node), .out_3(pull_resistor_18_node));
  trnsstr trnsstr_22 (.in_1(A_8), .in_2(1'b1), .out_3(trnsstr_22_out_3));
  trnsstr trnsstr_23 (.in_1(B_6), .in_2(1'b1), .out_3(trnsstr_22_out_3));
  Pull_Resistor pull_resistor_19 (.node(trnsstr_22_out_3));
  nand nand_7 (nand_7_out, in_24, in_26);
  and and_4 (and_4_out, in_20, in_22);
  nor nor_7 (nor_7_out, in_20, in_22);
  nand nand_8 (nand_8_out, in_24, nand_7_out);
  nand nand_9 (nand_9_out, nand_7_out, in_26);
  nor nor_8 (nor_8_out, in_28, in_30);
  xnor xnor_1 (out_42, A_8, B_6);
  Pull_Resistor #(.pull(1)) pull_resistor_20 (.node(pull_resistor_20_node));
  trnsstr trnsstr_24 (.in_1(trnsstr_22_out_3), .in_2(1'b0), .out_3(pull_resistor_20_node));
  or or_4 (out_51, and_4_out, nor_7_out);
  nand nand_10 (nand_10_out, nand_8_out, nand_9_out);
  nor nor_9 (nor_9_out, in_28, nor_8_out);
  nor nor_10 (nor_10_out, nor_8_out, in_30);
  trnsstr trnsstr_25 (.in_1(pull_resistor_20_node), .in_2(1'b1), .out_3(out_45));
  nand nand_11 (out_53, nand_10_out, nand_10_out);
  nor nor_11 (out_54, nor_9_out, nor_10_out);
  trnsstr trnsstr_26 (.in_1(pull_resistor_18_node), .in_2(1'b1), .out_3(out_45));
  Pull_Resistor pull_resistor_21 (.node(out_45));

  assign out_43 = A_5;

  // Notes on the sheet:
  //   OUI / YES
  //   NON / NO
  //   OU / OR
  //   ET / AND
  //   NON-OU / NOR
  //   NON-ET / NAND
  //   Toutes
  //   NAND
  //   NOR
  //   OU-EXCLUSIF / XOR
  //   NON-OU-EXCLUSIF / XNOR
  //   Toutes
  //   NAND
  //   NOR
endmodule

module trnsstr (
  input  in_1,
  input  in_2,
  output out_3
);

  assign out_3 = in_1 ? in_2 : 1'bz;  // Controlled_Buffer controlled_buffer_1
endmodule
